# Fritzing sketch Circuit_Diagram (saved by Fritzing 0.9.3b)
breadboards: 2

parts:
  U1 = attiny85 [package=dip]
  Part1 = Bluetooth HC-05 Macho
  Part2 = Bluetooth HC-05 Macho
  IC1 = Voltage Regulator [package=to220-igo]
  C1 = Electrolytic Capacitor [capacitance=10μF package="0605 [SMD, electrolytic]"]
  C2 = Tantalum Capacitor [capacitance=1μF package="200 mil [THT, tantalum]"]
  VCC1 = Battery block 9V
  LED1 = smd LED [color="Red (633nm)" package="0805 [SMD]"]
  U2 = attiny85 [package=dip]
  Part3 = Bluetooth HC-05 Macho
  IC2 = Voltage Regulator [package=to220-igo]
  C3 = Electrolytic Capacitor [capacitance=10μF package="0605 [SMD, electrolytic]"]
  C4 = Tantalum Capacitor [capacitance=1μF package="200 mil [THT, tantalum]"]
  VCC2 = Battery block 9V
  LED3 = LEDs [package=led10mm]

nets:
  N1: U1.Pin_2, LED1.anode
  N2: U1.Pin_3, Part2.RXD
  GND: U1.Pin_4, Part1.GND, Part2.GND, IC1.IN, C1.+, C2.-, VCC1.-, LED1.cathode
  N3: U1.Pin_6, Part1.TXD
  VCC: U1.Pin_8, Part1.VCC, Part2.VCC, IC1.OUT, C2.+
  N4: IC1.GND, C1.-, VCC1.+
  N5: U2.Pin_2, LED3.A
  N6: U2.Pin_4, Part3.GND, IC2.IN, C3.+, C4.-, VCC2.-, LED3.C
  N7: U2.Pin_6, Part3.TXD
  N8: U2.Pin_8, Part3.VCC, IC2.OUT, C4.+
  N9: IC2.GND, C3.-, VCC2.+

notes:
  Right Glove
  Left Glove
